// Logisim project 1st Canonical Form.circ as structural Verilog: 4 circuits, main circuit main
module main (
  input  A,
  input  B,
  input  C,
  output A_prime_BC_prime_ABC_prime_A_prime_B_prime_C
);

  wire n7404_1_out_9, n7404_1_out_10, n7404_1_out_11, n7411_1_out_12, n7411_1_out_13, n7411_1_out_14;

  _7404 u_7404_1 (
    .in_2(A), .in_3(B), .in_4(C), .out_10(n7404_1_out_10), .out_11(n7404_1_out_11), .out_9(n7404_1_out_9));  // open: in_1, in_5, in_6, in_7, in_8, out_12, out_13, out_14
  _7411 u_7411_1 (
    .in_4(C), .in_3(n7404_1_out_10), .out_12(n7411_1_out_12), .in_2(n7404_1_out_9), .in_5(A), .in_6(B),
    .in_7(n7404_1_out_11), .out_13(n7411_1_out_13), .in_8(n7404_1_out_9), .in_10(n7404_1_out_11),
    .out_14(n7411_1_out_14), .in_9(B));  // open: in_1, in_11
  _4075 u_4075_1 (
    .in_5(n7411_1_out_14), .in_6(n7411_1_out_13), .out_13(A_prime_BC_prime_ABC_prime_A_prime_B_prime_C),
    .in_7(n7411_1_out_12));  // open: in_2, in_3, in_4, out_12, in_8, in_9, out_14, in_10, in_1, in_11

  // Notes on the sheet:
  //   A'
  //   B'
  //   C'
  //   A'BC'
  //   ABC'
  //   A'B'C
endmodule

module _7411 (
  input  in_1,
  input  in_2,
  input  in_3,
  input  in_4,
  input  in_5,
  input  in_6,
  input  in_7,
  input  in_8,
  input  in_9,
  input  in_10,
  input  in_11,
  output out_12,
  output out_13,
  output out_14
);

  and and_1 (out_12, in_2, in_3, in_4);
  and and_2 (out_13, in_5, in_6, in_7);
  and and_3 (out_14, in_8, in_9, in_10);
endmodule

module _4075 (
  input  in_1,
  input  in_2,
  input  in_3,
  input  in_4,
  input  in_5,
  input  in_6,
  input  in_7,
  input  in_8,
  input  in_9,
  input  in_10,
  input  in_11,
  output out_12,
  output out_13,
  output out_14
);

  or or_1 (out_12, in_2, in_3, in_4);
  or or_2 (out_13, in_5, in_6, in_7);
  or or_3 (out_14, in_8, in_9, in_10);
endmodule

module _7404 (
  input  in_1,
  input  in_2,
  input  in_3,
  input  in_4,
  input  in_5,
  input  in_6,
  input  in_7,
  input  in_8,
  output out_9,
  output out_10,
  output out_11,
  output out_12,
  output out_13,
  output out_14
);

  not not_1 (out_9, in_2);
  not not_2 (out_10, in_3);
  not not_3 (out_11, in_4);
  not not_4 (out_12, in_5);
  not not_5 (out_13, in_6);
  not not_6 (out_14, in_7);
endmodule
