// Logisim project BCD to Excess-3 Converter.circ as structural Verilog: 4 circuits, main circuit main
module main (
  input  W,
  input  X,
  input  Y,
  input  Z,
  output A,
  output B,
  output C,
  output D
);

  wire ic_7404_1_out_9, ic_7404_1_out_10, ic_7404_1_out_11, ic_7408_1_out_11, ic_7408_1_out_12,
       ic_7408_1_out_13, ic_7408_1_out_14, ic_7408_2_out_11, ic_7408_2_out_12, ic_7408_2_out_14,
       ic_7432_1_out_11, ic_7432_1_out_14;

  IC_7404 ic_7404_1 (
    .in_1(W), .in_2(X), .in_3(Y), .in_4(Z), .out_9(ic_7404_1_out_9), .out_10(ic_7404_1_out_10),
    .out_11(ic_7404_1_out_11), .out_12(D));  // open: in_5, in_6, in_7, in_8, out_13, out_14
  IC_7408 ic_7408_1 (
    .in_1(X), .in_2(Y), .in_3(X), .in_4(Z), .in_5(D), .in_6(ic_7404_1_out_11), .in_7(ic_7408_1_out_13),
    .in_8(X), .out_11(ic_7408_1_out_11), .out_12(ic_7408_1_out_12), .out_13(ic_7408_1_out_13),
    .out_14(ic_7408_1_out_14));  // open: in_9, in_10
  IC_7432 ic_7432_1 (
    .in_1(ic_7408_1_out_12), .in_2(ic_7408_1_out_11), .in_3(ic_7432_1_out_11), .in_4(W),
    .in_5(ic_7408_1_out_14), .in_6(ic_7432_1_out_14), .in_7(ic_7408_2_out_11), .in_8(ic_7408_2_out_12),
    .out_11(ic_7432_1_out_11), .out_12(A), .out_13(B), .out_14(ic_7432_1_out_14));  // open: in_9, in_10
  IC_7432 ic_7432_2 (
    .in_7(ic_7408_2_out_14), .in_8(ic_7408_1_out_13), .out_14(C));  // open: in_1, in_2, in_3, in_4, in_5, in_6, in_9, in_10, out_11, out_12, out_13
  IC_7408 ic_7408_2 (
    .in_1(Z), .in_2(ic_7404_1_out_10), .in_3(Y), .in_4(ic_7404_1_out_10), .in_7(Z), .in_8(Y),
    .out_11(ic_7408_2_out_11), .out_12(ic_7408_2_out_12), .out_14(ic_7408_2_out_14));  // open: in_5, in_6, in_9, in_10, out_13

  // Notes on the sheet:
  //   Fig: BCD to Excess-3 Converter
endmodule

module IC_7404 (
  input  in_1,
  input  in_2,
  input  in_3,
  input  in_4,
  input  in_5,
  input  in_6,
  input  in_7,
  input  in_8,
  output out_9,
  output out_10,
  output out_11,
  output out_12,
  output out_13,
  output out_14
);

  not not_1 (out_9, in_1);
  not not_2 (out_10, in_2);
  not not_3 (out_11, in_3);
  not not_4 (out_12, in_4);
  not not_5 (out_13, in_5);
  not not_6 (out_14, in_6);
endmodule

module IC_7408 (
  input  in_1,
  input  in_2,
  input  in_3,
  input  in_4,
  input  in_5,
  input  in_6,
  input  in_7,
  input  in_8,
  input  in_9,
  input  in_10,
  output out_11,
  output out_12,
  output out_13,
  output out_14
);

  and and_1 (out_11, in_1, in_2);
  and and_2 (out_12, in_3, in_4);
  and and_3 (out_13, in_5, in_6);
  and and_4 (out_14, in_7, in_8);
endmodule

module IC_7432 (
  input  in_1,
  input  in_2,
  input  in_3,
  input  in_4,
  input  in_5,
  input  in_6,
  input  in_7,
  input  in_8,
  input  in_9,
  input  in_10,
  output out_11,
  output out_12,
  output out_13,
  output out_14
);

  or or_1 (out_11, in_1, in_2);
  or or_2 (out_12, in_3, in_4);
  or or_3 (out_13, in_5, in_6);
  or or_4 (out_14, in_7, in_8);
endmodule
