// Logisim project Logic Diagram.circ as structural Verilog: 1 circuit, main circuit main
module main (
  input  W,
  input  X,
  input  Y,
  input  in_4,
  output A,
  output B,
  output C,
  output D_Z_prime
);

  wire and_1_out, and_2_out, and_3_out, and_4_out, and_5_out, and_6_out, and_7_out, not_1_out, not_2_out,
       not_3_out, or_1_out, or_3_out;

  not not_1 (not_1_out, W);
  not not_2 (not_2_out, X);
  not not_3 (not_3_out, Y);
  not not_4 (D_Z_prime, in_4);
  and and_1 (and_1_out, X, in_4);
  or or_1 (or_1_out, and_1_out, and_2_out);
  and and_2 (and_2_out, X, Y);
  and and_3 (and_3_out, not_2_out, in_4);
  and and_4 (and_4_out, not_2_out, Y);
  and and_5 (and_5_out, D_Z_prime, not_3_out);
  and and_6 (and_6_out, and_5_out, X);
  and and_7 (and_7_out, Y, in_4);
  or or_2 (A, or_1_out, W);
  or or_3 (or_3_out, and_3_out, and_4_out);
  or or_4 (B, or_3_out, and_6_out);
  or or_5 (C, and_5_out, and_7_out);

  // Notes on the sheet:
  //   Z
  //   Fig :Bollean logic diagram for  BCD to Excess-3 converter
  //   D
  //   A=W+XZ+XY
  //   B=X'Z+X'Y+XY'Z'
  //   C=Y'Z'+YZ
endmodule
