// Logisim project 4-bit Adder-Subtractor.circ as structural Verilog: 3 circuits, main circuit main
module main (
  input  M,
  input  A1,
  input  A2,
  input  A3,
  input  A4,
  input  B1,
  input  B2,
  input  B3,
  input  B4,
  output C,
  output S1,
  output S2,
  output S3,
  output S4
);

  wire ic_7486_1_out_11, ic_7486_1_out_12, ic_7486_1_out_13, ic_7486_1_out_14;

  IC_74283 ic_74283_1 (
    .A1(A1), .A2(ic_7486_1_out_12), .A3(ic_7486_1_out_14), .A4(A4), .in_9(M), .out_12(C), .out_13(S1),
    .out_14(S2), .out_15(S3), .out_16(S4), .B1(ic_7486_1_out_11), .B2(A2), .b3(A3), .B4(ic_7486_1_out_13));  // open: in_10, in_11
  IC_7486 ic_7486_1 (
    .in_1(M), .in_2(B1), .in_3(M), .in_4(B2), .in_5(B4), .in_6(M), .in_7(M), .in_8(B3),
    .out_11(ic_7486_1_out_11), .out_12(ic_7486_1_out_12), .out_13(ic_7486_1_out_13), .out_14(ic_7486_1_out_14));  // open: in_9, in_10

  // Notes on the sheet:
  //   Figure:4-bit Adder-Subtractor
endmodule

module IC_74283 (
  input  A1,
  input  A2,
  input  A3,
  input  A4,
  input  B1,
  input  B2,
  input  b3,
  input  B4,
  input  in_9,
  input  in_10,
  input  in_11,
  output out_12,
  output out_13,
  output out_14,
  output out_15,
  output out_16
);

  wire adder_1_cout, adder_2_cout, adder_3_cout;

  Adder #(.width(1)) adder_1 (.a(A4), .b(B4), .out(out_16), .cin(in_9), .cout(adder_1_cout));
  Adder #(.width(1)) adder_2 (.a(A3), .b(b3), .out(out_15), .cin(adder_1_cout), .cout(adder_2_cout));
  Adder #(.width(1)) adder_3 (.a(A2), .b(B2), .out(out_14), .cin(adder_2_cout), .cout(adder_3_cout));
  Adder #(.width(1)) adder_4 (.a(A1), .b(B1), .out(out_13), .cin(adder_3_cout), .cout(out_12));
endmodule

module IC_7486 (
  input  in_1,
  input  in_2,
  input  in_3,
  input  in_4,
  input  in_5,
  input  in_6,
  input  in_7,
  input  in_8,
  input  in_9,
  input  in_10,
  output out_11,
  output out_12,
  output out_13,
  output out_14
);

  xor xor_1 (out_11, in_1, in_2);
  xor xor_2 (out_12, in_3, in_4);
  xor xor_3 (out_13, in_5, in_6);
  xor xor_4 (out_14, in_7, in_8);
endmodule
