// Logisim project BCD Adder.circ as structural Verilog: 4 circuits, main circuit main
module main (
  input  in_1,
  input  A,
  input  A2,
  input  A3,
  input  A4,
  input  B1,
  input  B2,
  input  B3,
  input  B4,
  output C,
  output S1,
  output S2,
  output S3,
  output S4
);

  wire ic_7408_1_out_11, ic_7408_1_out_12, ic_7432_1_out_11, ic_74283_1_out_12, ic_74283_1_out_13,
       ic_74283_1_out_14, ic_74283_1_out_15, ic_74283_1_out_16;

  IC_74283 ic_74283_1 (
    .in_2(B1), .in_3(B2), .in_4(B3), .in_5(B4), .in_1(in_1), .out_12(ic_74283_1_out_12),
    .out_13(ic_74283_1_out_13), .out_14(ic_74283_1_out_14), .out_15(ic_74283_1_out_15),
    .out_16(ic_74283_1_out_16), .in_6(A), .in_7(A2), .in_8(A3), .in_9(A4));  // open: in_10, in_11
  IC_7408 ic_7408_1 (
    .in_1(ic_74283_1_out_13), .in_2(ic_74283_1_out_15), .in_3(ic_74283_1_out_13), .in_4(ic_74283_1_out_14),
    .out_11(ic_7408_1_out_11), .out_12(ic_7408_1_out_12));  // open: in_5, in_6, in_7, in_8, in_9, in_10, out_13, out_14
  IC_74283 ic_74283_2 (
    .in_2(ic_74283_1_out_13), .in_3(ic_74283_1_out_14), .in_4(ic_74283_1_out_15), .in_5(ic_74283_1_out_16),
    .in_1(in_1), .out_13(S1), .out_14(S2), .out_15(S3), .out_16(S4), .in_6(in_1), .in_7(C), .in_8(C),
    .in_9(in_1));  // open: in_10, in_11, out_12
  IC_7432 ic_7432_1 (
    .in_1(ic_7408_1_out_11), .in_2(ic_7408_1_out_12), .in_3(ic_7432_1_out_11), .in_4(ic_74283_1_out_12),
    .out_11(ic_7432_1_out_11), .out_12(C));  // open: in_5, in_6, in_7, in_8, in_9, in_10, out_13, out_14

  // Notes on the sheet:
  //   Figure:BCD Adder circuit
endmodule

module IC_7408 (
  input  in_1,
  input  in_2,
  input  in_3,
  input  in_4,
  input  in_5,
  input  in_6,
  input  in_7,
  input  in_8,
  input  in_9,
  input  in_10,
  output out_11,
  output out_12,
  output out_13,
  output out_14
);

  and and_1 (out_11, in_1, in_2);
  and and_2 (out_12, in_3, in_4);
  and and_3 (out_13, in_5, in_6);
  and and_4 (out_14, in_7, in_8);
endmodule

module IC_7432 (
  input  in_1,
  input  in_2,
  input  in_3,
  input  in_4,
  input  in_5,
  input  in_6,
  input  in_7,
  input  in_8,
  input  in_9,
  input  in_10,
  output out_11,
  output out_12,
  output out_13,
  output out_14
);

  or or_1 (out_11, in_1, in_2);
  or or_2 (out_12, in_3, in_4);
  or or_3 (out_13, in_5, in_6);
  or or_4 (out_14, in_7, in_8);
endmodule

module IC_74283 (
  input  in_1,
  input  in_2,
  input  in_3,
  input  in_4,
  input  in_5,
  input  in_6,
  input  in_7,
  input  in_8,
  input  in_9,
  input  in_10,
  input  in_11,
  output out_12,
  output out_13,
  output out_14,
  output out_15,
  output out_16
);

  wire adder_1_cout, adder_2_cout, adder_3_cout;

  Adder #(.width(1)) adder_1 (.a(in_5), .b(in_9), .out(out_16), .cin(in_1), .cout(adder_1_cout));
  Adder #(.width(1)) adder_2 (.a(in_4), .b(in_8), .out(out_15), .cin(adder_1_cout), .cout(adder_2_cout));
  Adder #(.width(1)) adder_3 (.a(in_3), .b(in_7), .out(out_14), .cin(adder_2_cout), .cout(adder_3_cout));
  Adder #(.width(1)) adder_4 (.a(in_2), .b(in_6), .out(out_13), .cin(adder_3_cout), .cout(out_12));
endmodule
