// Logisim project Constructing a Multiplexer using basic Logic Gates.circ as structural Verilog: 1 circuit, main circuit main
module main (
  input  A,
  input  B,
  input  in_3,
  input  E,
  output out_5
);

  wire and_1_out, and_2_out, and_3_out, and_4_out, and_5_out, and_6_out, and_7_out, and_8_out, not_1_out,
       not_2_out, or_1_out, or_3_out;

  not not_1 (not_1_out, A);
  not not_2 (not_2_out, B);
  and and_1 (and_1_out, not_1_out, not_2_out, 1'b1);
  and and_2 (and_2_out, not_1_out, B, 1'b1);
  and and_3 (and_3_out, A, not_2_out, in_3);
  and and_4 (and_4_out, A, B, in_3);
  and and_5 (and_5_out, and_1_out, E);
  and and_6 (and_6_out, and_2_out, E);
  and and_7 (and_7_out, and_3_out, E);
  and and_8 (and_8_out, and_4_out, E);
  or or_1 (or_1_out, and_5_out, and_6_out);
  or or_2 (out_5, or_1_out, or_3_out);
  or or_3 (or_3_out, and_7_out, and_8_out);

  // Notes on the sheet:
  //   Figure: Constructing a 4:1 Multiplexer using basic Logic Gates
endmodule
