// Logisim project Decoder.circ as structural Verilog: 3 circuits, main circuit main
module main (
  input  C,
  input  B,
  input  A,
  input  in_4,
  input  in_5,
  input  in_6,
  output out_7,
  output out_8,
  output out_9,
  output out_10,
  output out_11,
  output out_12,
  output out_13,
  output out_14
);

  wire ic_7404_1_out_9, ic_7404_1_out_10, ic_7404_1_out_11;

  IC_7404 ic_7404_1 (
    .in_1(C), .in_2(B), .in_3(A), .out_9(ic_7404_1_out_9), .out_10(ic_7404_1_out_10),
    .out_11(ic_7404_1_out_11));  // open: in_4, in_5, in_6, in_7, in_8, out_12, out_13, out_14
  IC_74138 ic_74138_1 (
    .out_9(out_7), .out_10(out_8), .out_11(out_9), .out_12(out_10), .out_13(out_11), .out_14(out_12),
    .out_15(out_13), .out_16(out_14), .A(A), .B(B), .C(C), .E1(in_4), .E2(in_5), .E3(in_6));  // open: in_7, in_8

  // Notes on the sheet:
  //   B'
  //   A'
  //   C'
endmodule

module IC_7404 (
  input  in_1,
  input  in_2,
  input  in_3,
  input  in_4,
  input  in_5,
  input  in_6,
  input  in_7,
  input  in_8,
  output out_9,
  output out_10,
  output out_11,
  output out_12,
  output out_13,
  output out_14
);

  not not_1 (out_9, in_1);
  not not_2 (out_10, in_2);
  not not_3 (out_11, in_3);
  not not_4 (out_12, in_4);
  not not_5 (out_13, in_5);
  not not_6 (out_14, in_6);
endmodule

module IC_74138 (
  input  E1,
  input  E2,
  input  E3,
  input  A,
  input  B,
  input  C,
  input  in_7,
  input  in_8,
  output out_9,
  output out_10,
  output out_11,
  output out_12,
  output out_13,
  output out_14,
  output out_15,
  output out_16
);

  wire and_1_out, decoder_1_out0, decoder_1_out1, decoder_1_out2, decoder_1_out3, decoder_1_out4,
       decoder_1_out5, decoder_1_out6, decoder_1_out7, not_1_out, not_2_out;

  not not_1 (not_1_out, E1);
  not not_2 (not_2_out, E2);
  and and_1 (and_1_out, not_1_out, not_2_out, E3);
  Decoder #(.select(3)) decoder_1 (
    .out0(decoder_1_out0), .out1(decoder_1_out1), .out2(decoder_1_out2), .out3(decoder_1_out3),
    .out4(decoder_1_out4), .out5(decoder_1_out5), .out6(decoder_1_out6), .out7(decoder_1_out7),
    .sel({A, B, C}), .en(and_1_out));
  not not_3 (out_9, decoder_1_out0);
  not not_4 (out_10, decoder_1_out1);
  not not_5 (out_11, decoder_1_out2);
  not not_6 (out_12, decoder_1_out3);
  not not_7 (out_13, decoder_1_out4);
  not not_8 (out_14, decoder_1_out5);
  not not_9 (out_15, decoder_1_out6);
  not not_10 (out_16, decoder_1_out7);

  // Notes on the sheet:
  //   enable Logic
endmodule
