// Logisim project Using a Multiplexer to implement a Boolean function.circ as structural Verilog: 1 circuit, main circuit main
module main (
  input  A,
  input  B,
  input  C,
  input  D,
  input  in_5,
  output Y
);

  Multiplexer #(.select(3)) multiplexer_1 (
    .in0(1'b1), .in1(D), .in2(D), .in3(in_5), .in4(1'b1), .in5(in_5), .in6(in_5), .in7(1'b1), .out(Y),
    .sel({A, B, C}), .en(1'b1));

  // Notes on the sheet:
  //   Figure: Using an 8:1 Multiplexer to implement a Boolean function
endmodule
