// Logisim project 7 Segment Display IC Diagram.circ as structural Verilog: 4 circuits, main circuit main
// B
module main (
  input  D,
  input  C,
  input  B,
  input  A,
  output a_2,
  output b_2,
  output c_2,
  output d_2,
  output e,
  output f,
  output g
);

  wire ic_7404_1_out_9, ic_7404_1_out_10, ic_7404_1_out_11, ic_7404_1_out_12, ic_7408_1_out_11,
       ic_7408_1_out_12, ic_7408_1_out_13, ic_7408_1_out_14, ic_7408_2_out_11, ic_7408_2_out_12,
       ic_7408_2_out_13, ic_7408_2_out_14, ic_7408_3_out_12, ic_7432_1_out_11, ic_7432_1_out_12,
       ic_7432_1_out_13, ic_7432_2_out_12, ic_7432_2_out_13, ic_7432_3_out_11, ic_7432_3_out_12,
       ic_7432_4_out_11, ic_7432_4_out_12, ic_7432_4_out_13, ic_7432_4_out_14;

  IC_7404 ic_7404_1 (
    .in_1(D), .in_2(C), .in_3(B), .in_4(A), .out_9(ic_7404_1_out_9), .out_10(ic_7404_1_out_10),
    .out_11(ic_7404_1_out_11), .out_12(ic_7404_1_out_12));  // open: in_5, in_6, in_7, in_8, out_13, out_14
  IC_7408 ic_7408_1 (
    .in_1(ic_7404_1_out_12), .in_2(ic_7404_1_out_10), .in_3(A), .in_4(C), .in_5(ic_7404_1_out_11),
    .in_6(ic_7404_1_out_12), .in_7(A), .in_8(B), .out_11(ic_7408_1_out_11), .out_12(ic_7408_1_out_12),
    .out_13(ic_7408_1_out_13), .out_14(ic_7408_1_out_14));  // open: in_9, in_10
  IC_7432 ic_7432_1 (
    .in_1(ic_7408_1_out_12), .in_2(ic_7408_1_out_11), .in_3(ic_7432_1_out_11), .in_4(D),
    .in_5(ic_7408_1_out_14), .in_6(ic_7408_1_out_13), .in_7(B), .in_8(ic_7432_1_out_12),
    .out_11(ic_7432_1_out_11), .out_12(ic_7432_1_out_12), .out_13(ic_7432_1_out_13), .out_14(a_2));  // open: in_9, in_10
  IC_7408 ic_7408_2 (
    .in_1(ic_7408_1_out_12), .in_2(ic_7404_1_out_11), .in_3(B), .in_4(ic_7404_1_out_10), .in_5(B),
    .in_6(ic_7404_1_out_12), .in_7(C), .in_8(ic_7404_1_out_12), .out_11(ic_7408_2_out_11),
    .out_12(ic_7408_2_out_12), .out_13(ic_7408_2_out_13), .out_14(ic_7408_2_out_14));  // open: in_9, in_10
  IC_7432 ic_7432_2 (
    .in_1(ic_7432_1_out_13), .in_2(ic_7404_1_out_10), .in_3(ic_7404_1_out_11), .in_4(C),
    .in_5(ic_7408_2_out_13), .in_6(ic_7408_1_out_11), .in_7(A), .in_8(ic_7432_2_out_12), .out_11(b_2),
    .out_12(ic_7432_2_out_12), .out_13(ic_7432_2_out_13), .out_14(c_2));  // open: in_9, in_10
  IC_7432 ic_7432_3 (
    .in_1(ic_7408_2_out_12), .in_2(ic_7432_3_out_12), .in_3(ic_7408_2_out_11), .in_4(ic_7432_2_out_13),
    .in_5(ic_7432_3_out_11), .in_6(D), .in_7(ic_7408_1_out_11), .in_8(ic_7408_2_out_13),
    .out_11(ic_7432_3_out_11), .out_12(ic_7432_3_out_12), .out_13(d_2), .out_14(e));  // open: in_9, in_10
  _7_Segment_Display u_7_segment_display_1 (.g(g), .f(f), .a(a_2), .b(b_2), .e(e), .d(d_2), .c(c_2));  // open: dp
  IC_7432 ic_7432_4 (
    .in_1(ic_7408_1_out_13), .in_2(ic_7408_2_out_14), .in_3(ic_7432_4_out_11), .in_4(D),
    .in_5(ic_7432_4_out_14), .in_6(D), .in_7(ic_7408_2_out_12), .in_8(ic_7408_2_out_13),
    .out_11(ic_7432_4_out_11), .out_12(ic_7432_4_out_12), .out_13(ic_7432_4_out_13), .out_14(ic_7432_4_out_14));  // open: in_9, in_10
  IC_7408 ic_7408_3 (
    .in_3(C), .in_4(ic_7404_1_out_11), .out_12(ic_7408_3_out_12));  // open: in_1, in_2, in_5, in_6, in_7, in_8, in_9, in_10, out_11, out_13, out_14
  IC_7432 ic_7432_5 (
    .in_1(ic_7432_4_out_13), .in_2(ic_7408_3_out_12), .in_3(ic_7408_3_out_12), .in_4(ic_7432_4_out_12),
    .out_11(g), .out_12(f));  // open: in_5, in_6, in_7, in_8, in_9, in_10, out_13, out_14

  // Notes on the sheet:
  //   A'C'
  //   AC
  //   B'AC
  //   BC'
  //   Fig: 7-Segment Display 
  //   A'B'
  //   AB
  //   BA'
  //   CA'
  //   B'C
endmodule

module IC_7404 (
  input  in_1,
  input  in_2,
  input  in_3,
  input  in_4,
  input  in_5,
  input  in_6,
  input  in_7,
  input  in_8,
  output out_9,
  output out_10,
  output out_11,
  output out_12,
  output out_13,
  output out_14
);

  not not_1 (out_9, in_1);
  not not_2 (out_10, in_2);
  not not_3 (out_11, in_3);
  not not_4 (out_12, in_4);
  not not_5 (out_13, in_5);
  not not_6 (out_14, in_6);
endmodule

module IC_7408 (
  input  in_1,
  input  in_2,
  input  in_3,
  input  in_4,
  input  in_5,
  input  in_6,
  input  in_7,
  input  in_8,
  input  in_9,
  input  in_10,
  output out_11,
  output out_12,
  output out_13,
  output out_14
);

  and and_1 (out_11, in_1, in_2);
  and and_2 (out_12, in_3, in_4);
  and and_3 (out_13, in_5, in_6);
  and and_4 (out_14, in_7, in_8);
endmodule

module IC_7432 (
  input  in_1,
  input  in_2,
  input  in_3,
  input  in_4,
  input  in_5,
  input  in_6,
  input  in_7,
  input  in_8,
  input  in_9,
  input  in_10,
  output out_11,
  output out_12,
  output out_13,
  output out_14
);

  or or_1 (out_11, in_1, in_2);
  or or_2 (out_12, in_3, in_4);
  or or_3 (out_13, in_5, in_6);
  or or_4 (out_14, in_7, in_8);
endmodule
