// Logisim project Constructing a Sequential Circuit using D Flip-Flops.circ as structural Verilog: 8 circuits, main circuit main
module main (
  input  Clock_Enable,
  input  X,
  input  SET,
  input  clear,
  output out_5,
  output A,
  output B
);

  wire ic_4072_1_out_13, ic_7404_1_out_9, ic_7404_1_out_13, ic_7404_1_out_14, ic_7411_1_out_12,
       ic_7411_2_out_12, ic_7411_2_out_13, ic_7411_2_out_14;

  IC_7404 ic_7404_1 (
    .in_1(X), .in_5(A), .in_6(B), .out_9(ic_7404_1_out_9), .out_13(ic_7404_1_out_13),
    .out_14(ic_7404_1_out_14));  // open: in_2, in_3, in_4, in_7, in_8, out_10, out_11, out_12
  Timer_555 timer_555_1 (.in_1(Clock_Enable), .out_4(out_5));  // open: in_2, in_3
  IC_7474 ic_7474_1 (
    .out_11(A), .out_12(B), .CLR(clear), .SET(SET), .in_5(ic_4072_1_out_13), .in_3(out_5), .in_10(clear),
    .in_8(SET), .in_6(ic_7404_1_out_14), .in_4(out_5));  // open: out_13, out_14, in_1, in_2
  IC_7411 ic_7411_1 (
    .in_1(A), .in_2(X), .in_3(B), .out_12(ic_7411_1_out_12));  // open: in_4, in_5, in_6, in_7, in_8, in_9, out_13, out_14, in_10, in_11
  IC_7411 ic_7411_2 (
    .in_1(ic_7404_1_out_13), .in_2(ic_7404_1_out_14), .in_3(X), .in_4(ic_7404_1_out_9),
    .in_5(ic_7404_1_out_14), .in_6(A), .in_7(ic_7404_1_out_9), .in_8(B), .in_9(ic_7404_1_out_13),
    .out_12(ic_7411_2_out_12), .out_13(ic_7411_2_out_13), .out_14(ic_7411_2_out_14));  // open: in_10, in_11
  IC_4072 ic_4072_1 (
    .in_3(ic_7411_2_out_13), .in_4(ic_7411_2_out_14), .in_5(ic_7411_2_out_12), .in_6(ic_7411_1_out_12),
    .out_13(ic_4072_1_out_13));  // open: in_1, in_2, in_7, in_8, in_9, in_10, in_11, in_12, out_14

  // Notes on the sheet:
  //   Figure: 3.1 
  //   ABX
  //   AB'X'
  //   A'B'X
  //   A'BX
endmodule

module IC_4072 (
  input  in_1,
  input  in_2,
  input  in_3,
  input  in_4,
  input  in_5,
  input  in_6,
  input  in_7,
  input  in_8,
  input  in_9,
  input  in_10,
  input  in_11,
  input  in_12,
  output out_13,
  output out_14
);

  or or_1 (out_13, in_3, in_4, in_5, in_6);
  or or_2 (out_14, in_7, in_8, in_9, in_10);
endmodule

module IC_7404 (
  input  in_1,
  input  in_2,
  input  in_3,
  input  in_4,
  input  in_5,
  input  in_6,
  input  in_7,
  input  in_8,
  output out_9,
  output out_10,
  output out_11,
  output out_12,
  output out_13,
  output out_14
);

  not not_1 (out_9, in_1);
  not not_2 (out_10, in_2);
  not not_3 (out_11, in_3);
  not not_4 (out_12, in_4);
  not not_5 (out_13, in_5);
  not not_6 (out_14, in_6);
endmodule

module IC_7408 (
  input  in_1,
  input  in_2,
  input  in_3,
  input  in_4,
  input  in_5,
  input  in_6,
  input  in_7,
  input  in_8,
  input  in_9,
  input  in_10,
  output out_11,
  output out_12,
  output out_13,
  output out_14
);

  and and_1 (out_11, in_1, in_2);
  and and_2 (out_12, in_3, in_4);
  and and_3 (out_13, in_5, in_6);
  and and_4 (out_14, in_7, in_8);
endmodule

module IC_7432 (
  input  in_1,
  input  in_2,
  input  in_3,
  input  in_4,
  input  in_5,
  input  in_6,
  input  in_7,
  input  in_8,
  input  in_9,
  input  in_10,
  output out_11,
  output out_12,
  output out_13,
  output out_14
);

  or or_1 (out_11, in_1, in_2);
  or or_2 (out_12, in_3, in_4);
  or or_3 (out_13, in_5, in_6);
  or or_4 (out_14, in_7, in_8);
endmodule

module IC_7411 (
  input  in_1,
  input  in_2,
  input  in_3,
  input  in_4,
  input  in_5,
  input  in_6,
  input  in_7,
  input  in_8,
  input  in_9,
  input  in_10,
  input  in_11,
  output out_12,
  output out_13,
  output out_14
);

  and and_1 (out_12, in_1, in_2, in_3);
  and and_2 (out_13, in_4, in_5, in_6);
  and and_3 (out_14, in_7, in_8, in_9);
endmodule

module Timer_555 (
  input  in_1,
  input  in_2,
  input  in_3,
  output out_4
);

  wire clock_1_out;

  Clock clock_1 (.out(clock_1_out));
  and and_1 (out_4, in_1, clock_1_out);
endmodule

module IC_7474 (
  input  in_1,
  input  in_2,
  input  in_3,
  input  in_4,
  input  in_5,
  input  in_6,
  input  SET,
  input  in_8,
  input  CLR,
  input  in_10,
  output out_11,
  output out_12,
  output out_13,
  output out_14
);

  wire not_1_out, not_2_out, not_3_out, not_4_out;

  not not_1 (not_1_out, CLR);
  not not_2 (not_2_out, SET);
  D_Flip_Flop d_ff_1 (
    .clk(in_3), .D(in_5), .Q(out_11), .Qn(out_13), .en(not_2_out), .reset(not_1_out));  // open: preset
  not not_3 (not_3_out, in_8);
  not not_4 (not_4_out, in_10);
  D_Flip_Flop d_ff_2 (
    .clk(in_4), .D(in_6), .Q(out_12), .Qn(out_14), .en(not_3_out), .reset(not_4_out));  // open: preset
endmodule
